// Logisim project miniARM.circ as structural Verilog: 1 circuit, main circuit main
module main (
);

  wire clock_1_out, control_unit_1_p10, HPC, HR, HRADM, HRI, HSR, MemB, not_1_out, not_2_out, PCA,
       register_file_1_p8, Reset_PC_out, Reset_Registers_out, RW;
  wire [1:0] RI_q;
  wire [2:0] Rx, Ry, Rz;
  wire [3:0] SR_q, undriven;
  wire [3:1] CodeUAL;
  wire [4:0] OpCode;
  wire [15:0] controlled_buffer_1_out, controlled_buffer_2_out, PC_q, RADM_q, ram_1_data, register_file_1_p5,
       register_file_1_p6, register_file_1_p7;

  Register #(.width(16)) RADM (.D(register_file_1_p6), .Q(RADM_q), .clk(HRADM));  // open: en, clr
  assign controlled_buffer_1_out = MemB ? ram_1_data : 16'bz;  // Controlled_Buffer controlled_buffer_1
  RAM #(.addrWidth(16), .dataWidth(16), .bus("separate")) ram_1 (
    .addr(RADM_q), .din(register_file_1_p6), .data(ram_1_data), .clk(RW));  // open: str, sel, ld, clr
  Register #(.width(16)) RI (.D(ram_1_data), .Q({OpCode, Rx, Ry, Rz, RI_q}), .clk(HRI));  // open: en, clr
  Register #(.width(16)) PC (.D(register_file_1_p6), .Q(PC_q), .clk(HPC), .clr(Reset_PC_out));  // open: en
  assign controlled_buffer_2_out = PCA ? PC_q : 16'bz;  // Controlled_Buffer controlled_buffer_2
  Button Reset_PC (.out(Reset_PC_out));
  assign controlled_buffer_1_out = not_1_out ? register_file_1_p7 : 16'bz;  // Controlled_Buffer controlled_buffer_3
  assign controlled_buffer_2_out = not_2_out ? register_file_1_p5 : 16'bz;  // Controlled_Buffer controlled_buffer_4
  not not_1 (not_1_out, MemB);
  not not_2 (not_2_out, PCA);
  // Register_File register_file_1: pin names not known; wires that end beside it: Ry, Rz, Rx, HR, register_file_1_p5, register_file_1_p6, register_file_1_p7, register_file_1_p8, CodeUAL[1], controlled_buffer_2_out, CodeUAL[2], CodeUAL[3]
  not not_3 (register_file_1_p8, Reset_Registers_out);
  Button Reset_Registers (.out(Reset_Registers_out));
  // ALU alu_1: pin names not known; wires that end beside it: register_file_1_p6, undriven[3], controlled_buffer_1_out, undriven[2], undriven[1]
  Register #(.width(4)) SR (.D(undriven), .Q(SR_q), .clk(HSR));  // open: en, clr
  Clock clock_1 (.out(clock_1_out));
  // Control_Unit control_unit_1: pin names not known; wires that end beside it: clock_1_out, HRADM, HRI, HR, HSR, HPC, RW, PCA, MemB, control_unit_1_p10, control_unit_1_p10
endmodule
